# Fritzing sketch lcd (saved by Fritzing 0.9.3b)
breadboards: 1

parts:
  part = Arduino Uno (Rev3)
  U1 = LCD-16X2 [package=lcd-16x2]
  R1 = Rotary Potentiometer (Large) [maximum_resistance=100kΩ package=THT]

nets:
  N1: part.D11_PWM/MOSI, U1.E
  N2: part.D12/MISO, U1.RS
  GND: part.GND, U1.VSS, U1.R_W, U1.K, R1.wiper
  N3: part.D2, U1.DB7
  N4: part.D3_PWM, U1.DB6
  N5: part.D4, U1.DB5
  N6: part.D5_PWM, U1.DB4
  N7: U1.VDD, U1.A
  N8: U1.VO, R1.leg1

notes:
  1
  16
