# Fritzing sketch looplicht (saved by Fritzing 0.9.3b)
breadboards: 1

parts:
  part = Arduino Uno (Rev3)
  R1 = Resistor [tolerance=±5% resistance=1k package=THT]
  R2 = Resistor [tolerance=±5% resistance=1k package=THT]
  R3 = Resistor [tolerance=±5% resistance=1k package=THT]
  R4 = Resistor [tolerance=±5% resistance=1k package=THT]
  R5 = Resistor [tolerance=±5% resistance=1k package=THT]
  R6 = Resistor [tolerance=±5% resistance=1k package=THT]
  R7 = Resistor [tolerance=±5% resistance=1k package=THT]
  R9 = Resistor [tolerance=±5% resistance=1k package=THT]
  LED2 = smd LED [color="Red (633nm)" package="0805 [SMD]"]
  LED3 = smd LED [color="Red (633nm)" package="0805 [SMD]"]
  LED6 = smd LED [color="Red (633nm)" package="0805 [SMD]"]
  LED7 = smd LED [color="Red (633nm)" package="0805 [SMD]"]
  LED8 = smd LED [color="Red (633nm)" package="0805 [SMD]"]
  LED9 = smd LED [color="Red (633nm)" package="0805 [SMD]"]
  LED5 = smd LED [color="Red (633nm)" package="0805 [SMD]"]
  LED4 = smd LED [color="Red (633nm)" package="0805 [SMD]"]

nets:
  N1: part.D8, R9.Pin_1
  N2: part.D9_PWM, R7.Pin_1
  N3: part.GND, LED2.cathode, LED3.cathode, LED6.cathode, LED7.cathode, LED8.cathode, LED9.cathode, LED5.cathode, LED4.cathode
  N4: part.D2, R1.Pin_1
  N5: part.D3_PWM, R2.Pin_1
  N6: part.D4, R3.Pin_1
  N7: part.D5_PWM, R6.Pin_1
  N8: part.D6_PWM, R4.Pin_1
  N9: part.D7, R5.Pin_1
  N10: R1.Pin_0, LED2.anode
  N11: R2.Pin_0, LED3.anode
  N12: R3.Pin_0, LED4.anode
  N13: R4.Pin_0, LED6.anode
  N14: R5.Pin_0, LED7.anode
  N15: R6.Pin_0, LED5.anode
  N16: R7.Pin_0, LED9.anode
  N17: R9.Pin_0, LED8.anode
